# Fritzing sketch MysteryMachineStandalone (saved by Fritzing 0.8.7b)
circuit board: 5cm x 8cm
breadboards: 1

parts:
  LED2_1 = LED - 5mm [color="Red (633nm)" package="5 mm [THT]"]
  LED2_2 = LED - 5mm [color="Yellow (595nm)" package="5 mm [THT]"]
  RH2 = Resistor [tolerance=±5% resistance=1M package=THT]
  RHM = Resistor [tolerance=±5% resistance=1M package=THT]
  RH1 = Resistor [tolerance=±5% resistance=1M package=THT]
  LED2_3 = LED - 5mm [color="Green (570nm)" package="5 mm [THT]"]
  R2 = Resistor [tolerance=±5% resistance=220 package=THT]
  LED1_1 = LED - 5mm [color="Red (633nm)" package="5 mm [THT]"]
  LED1_2 = LED - 5mm [color="Yellow (595nm)" package="5 mm [THT]"]
  LED1_3 = LED - 5mm [color="Green (555nm)" package="5 mm [THT]"]
  LEDM_3 = LED - 5mm [color="Red (633nm)" package="5 mm [THT]"]
  LEDM_2 = LED - 5mm [color="Red (633nm)" package="5 mm [THT]"]
  LEDM_1 = LED - 5mm [color="Red (633nm)" package="5 mm [THT]"]
  RM = Resistor [tolerance=±5% resistance=220 package=THT]
  R1 = Resistor [tolerance=±5% resistance=220 package=THT]
  U2 = atmega328 [package=dip]
  C4 = Capacitor [package=cap-pth-small2]
  C5 = Capacitor [package=cap-pth-small2]
  Y2 = CRYSTAL [package=crystal-smd-10.5x4.8-2pin]
  VCC = Battery
  R3 = Resistor [tolerance=±5% resistance=1k package=THT]
  Touch1 = Resistor [tolerance=±5% resistance=0 package=THT]
  TouchMid1 = Resistor [tolerance=±5% resistance=0 package=THT]
  RSM = Resistor [tolerance=±5% resistance=1k package=THT]
  RS2 = Resistor [tolerance=±5% resistance=1k package=THT]
  Touch2 = Resistor [tolerance=±5% resistance=0 package=THT]

nets:
  N1: LED2_1.cathode, LED2_2.cathode, LED2_3.cathode, R2.Pin_1
  N2: LED2_1.anode, U2.D9_(PWM)
  N3: LED2_2.anode, U2.D10_(PWM)
  N4: RH2.Pin_0, U2.D4, RS2.Pin_0
  N5: RH2.Pin_1, U2.D5_(PWM)
  N6: RHM.Pin_0, U2.A5
  N7: RHM.Pin_1, U2.A4, RSM.Pin_0
  N8: RH1.Pin_0, U2.D3_(PWM)
  N9: RH1.Pin_1, U2.D2, R3.Pin_0
  N10: LED2_3.anode, U2.D11_(PWM)
  N11: R2.Pin_0, RM.Pin_0, R1.Pin_0, U2.GND, C4.1, C5.2, VCC.-
  N12: LED1_1.cathode, LED1_2.cathode, LED1_3.cathode, R1.Pin_1
  N13: LED1_1.anode, U2.D6_(PWM)
  N14: LED1_2.anode, U2.D7
  N15: LED1_3.anode, U2.D8
  N16: LEDM_3.cathode, LEDM_2.cathode, LEDM_1.cathode, RM.Pin_1
  N17: LEDM_3.anode, U2.A2
  N18: LEDM_2.anode, U2.A1
  N19: LEDM_1.anode, U2.A0
  N20: U2.VCC, U2.AVCC, U2.AREF, VCC.+
  N21: U2.XLAT1, C4.2, Y2.2
  N22: U2.XLAT2, C5.1, Y2.1
  N23: R3.Pin_1, Touch1.Pin_0
  N24: TouchMid1.Pin_0, RSM.Pin_1
  N25: RS2.Pin_1, Touch2.Pin_1

notes:
  Capacitors: 22 pF
  Crystal: 16 MHz
